# Fritzing sketch ae-kit45-keypad4x3-pico (saved by Fritzing 0.9.6b)
breadboards: 1

parts:
  Mod1 = Raspberry Pi Pico
  J5 = Camdenboss CTB0158-8 [part_number=CTB0158-8 package=THT]

nets:
  N1: Mod1.pin_4, J5.terminal_2
  N2: Mod1.pin_5, J5.terminal_3
  N3: Mod1.pin_6, J5.terminal_4
  N4: Mod1.pin_9, J5.terminal_5
  N5: Mod1.pin_10, J5.terminal_6
  N6: Mod1.pin_11, J5.terminal_7
  N7: Mod1.pin_12, J5.terminal_8
  N8: Mod1.pin_37, J5.terminal_1

notes:
  秋月電子 AE-KIT45-KEYPAD4X3
  4x3 キーパッド作成キット

custom parts:
  Raspberry Pi Pico: Raspberry Pi Pico. Based around the RP2040 microcontroller the Pico is a low cost microcontroller device bringing Raspberry Pi quality, cost, and easy of use to the microcontroller space. Jan 2021, Split part in to two versions: tht (this one) and SMD. This one will drill holes for a .1 in header in pcb to allow plugging in the module as well as providing pads to solder the module to the top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
