# Fritzing sketch pico-ssd1306 (saved by Fritzing 0.9.6b)
circuit board: 8.46667cm x 5.64444cm
breadboards: 1

parts:
  128x64_I2C_OLED1 = 128x64 OLED I2C Graphic Display [package=DIP]
  Mod1 = Raspberry Pi Pico
  S1 = Pushbutton [package="[THT]"]
  S2 = Pushbutton [package="[THT]"]

nets:
  N1: 128x64_I2C_OLED1.SDA, Mod1.pin_21
  N2: 128x64_I2C_OLED1.SCL, Mod1.pin_22
  N3: 128x64_I2C_OLED1.GND, Mod1.pin_3, Mod1.pin_8, Mod1.pin_13, Mod1.pin_18, Mod1.pin_23, Mod1.pin_28, Mod1.pin_33, Mod1.pin_38, Mod1.pin_42, S1.Pin_3, S1.Pin_4, S2.Pin_3, S2.Pin_4
  N4: 128x64_I2C_OLED1.VCC, Mod1.pin_36
  N5: Mod1.pin_19, S2.Pin_1, S2.Pin_2
  N6: Mod1.pin_20, S1.Pin_1, S1.Pin_2

custom parts:
  128x64 OLED I2C Graphic Display: I2C 128x64 pixel OLED Graphic Display screen
  Raspberry Pi Pico: Raspberry Pi Pico. Based around the RP2040 microcontroller the Pico is a low cost microcontroller device bringing Raspberry Pi quality, cost, and easy of use to the microcontroller space. Jan 2021, Split part in to two versions: tht (this one) and SMD. This one will drill holes for a .1 in header in pcb to allow plugging in the module as well as providing pads to solder the module to the top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
